# Fritzing sketch intelliroads (saved by Fritzing 0.9.0b)
breadboards: 1

parts:
  S2 = Reed switch [package=THT]
  R2 = Resistor [tolerance=±5% resistance=10k package="0805 [SMD]"]
  S1 = Reed switch [package=THT]
  R1 = Resistor [tolerance=±5% resistance=10k package="0805 [SMD]"]
  Part1 = Arduino Uno (Rev3)

nets:
  N1: S2.pin_1, R2.Pin_0, Part1.D8
  N2: S2.pin_2, S1.pin_2, Part1.5V
  N3: R2.Pin_1, R1.Pin_0, Part1.GND
  N4: S1.pin_1, R1.Pin_1, Part1.D7
